# Fritzing sketch Flex Schematic PCB Breadboard (saved by Fritzing 0.8.5b)
circuit board: 8.46667cm x 5.64444cm
breadboards: 1

parts:
  Arduino_UNO_rev_3 = Arduino Uno (Rev3)
  R1 = Basic Flex Resistor
  R2 = Basic Flex Resistor
  J1 = Piezo Speaker
  R3 = Resistor [tolerance=±5% resistance=10k package=THT]
  R4 = Resistor [tolerance=±5% resistance=10k package=THT]

nets:
  N1: Arduino_UNO_rev_3.A0, Arduino_UNO_rev_3.A1, Arduino_UNO_rev_3.3V3, R3.Pin_1, R4.Pin_1
  N2: Arduino_UNO_rev_3.D8, J1.pin2
  5V/GND: Arduino_UNO_rev_3.GND, R1.pin_1, R2.pin_1, J1.pin1
  N3: R1.Pin_2, R4.Pin_0
  N4: R2.Pin_2, R3.Pin_0

notes:
  Zensah Flex Hack
  Left
  Right
